# Fritzing sketch 4Role4Button (saved by Fritzing 0.9.2b)
breadboards: 1

parts:
  Eleman1 = Arduino Mega 2560 (Rev3)
  S1 = Pushbutton [package="[THT]"]
  S2 = Pushbutton [package="[THT]"]
  S3 = Pushbutton [package="[THT]"]
  S4 = Pushbutton [package="[THT]"]
  U1 = 4-Channel 5v Relay Shield [package=relay-4ch5v10a]

nets:
  N1: Eleman1.D8_PWM, U1.IN4
  5V: Eleman1.5V, U1.VCC
  GND: Eleman1.GND, S1.Pin_1, S2.Pin_1, S3.Pin_1, S3.Pin_2, S4.Pin_1, S4.Pin_2, U1.GND
  N2: Eleman1.D1_TX0, S1.Pin_3, S1.Pin_4
  N3: Eleman1.D2_PWM, S2.Pin_3, S2.Pin_4
  N4: Eleman1.D3_PWM, S3.Pin_3, S3.Pin_4
  N5: Eleman1.D4_PWM, S4.Pin_3, S4.Pin_4
  N6: Eleman1.D5_PWM, U1.IN1
  N7: Eleman1.D6_PWM, U1.IN2
  N8: Eleman1.D7_PWM, U1.IN3

custom parts:
  4-Channel 5v Relay Shield: 4 Channel 5v Relay Shield w. 2x SPD-06VDC-SD-C
