# Fritzing sketch HC_SR501_PIR_sensoru (saved by Fritzing 0.9.2b)

parts:
  Eleman1 = HC-SR501 Body Sensor Module
  Eleman2 = Arduino Nano (Rev3.0)
  J1 = Piezo Speaker

nets:
  VCC: Eleman1.VCC, Eleman2.5V
  N1: Eleman1.OUT, Eleman2.D4
  GND: Eleman1.GND, Eleman2.GND, J1.pin1
  N2: Eleman2.D13/SCK, J1.pin2

custom parts:
  HC-SR501 Body Sensor Module: Pyroelectric Infrared PIR Motion Sensor Detector Module
