# Fritzing sketch gy_keypad (saved by Fritzing 0.9.2b)

parts:
  Matrix_keypad1 = KEYPAD 4x4
  Eleman1 = Arduino Nano (Rev3.0)

nets:
  N1: Matrix_keypad1.col1, Eleman1.D9
  N2: Matrix_keypad1.col2, Eleman1.D8
  N3: Matrix_keypad1.col3, Eleman1.D7
  N4: Matrix_keypad1.col4, Eleman1.D6
  N5: Matrix_keypad1.row1, Eleman1.D5
  N6: Matrix_keypad1.row2, Eleman1.D4
  N7: Matrix_keypad1.row3, Eleman1.D3
  N8: Matrix_keypad1.row4, Eleman1.D2

custom parts:
  KEYPAD 4x4: Matrix keypad 16 buttons, 4 rows x 4 columns
