# Fritzing sketch gy_L298N (saved by Fritzing 0.9.3b)
breadboards: 1

parts:
  VCC1 = Battery
  M1 = DC Motor
  M2 = DC Motor
  S1 = H-Bridge with L298N
  Parça1 = Arduino Nano (Rev3.0) (ICSP)
  Parça2 = Thumb Joystick
  Parça3 = Thumb Joystick

nets:
  N1: VCC1.+, S1.12V
  N2: M1.pin_1, S1.M2-02
  N3: M1.pin_2, S1.M2-01
  N4: M2.pin_1, S1.M1-02
  N5: M2.pin_2, S1.M1-01
  GND: S1.GND, Parça2.GND, Parça3.GND
  N6: S1.ENA, Parça1.A0
  N7: S1.IN1, Parça1.D2
  N8: S1.IN2, Parça1.D3
  N9: S1.IN3, Parça1.D4
  N10: S1.IN4, Parça1.D5
  N11: S1.ENB, Parça1.A1
  VCC: Parça1.5V, Parça2.VCC, Parça3.VCC
  N12: Parça1.A3, Parça3.VERT
  N13: Parça1.A2, Parça2.VERT

custom parts:
  H-Bridge with L298N: h-bridge
