# Fritzing sketch Untitled Sketch (saved by Fritzing 0.9.2b)
breadboards: 1

parts:
  Eleman1 = Arduino Nano (Rev3.0)
  R1 = Photocell (LDR) [package=THT]  # not connected
  R2 = Resistor [tolerance=±5% resistance=220 package="0805 [SMD]"]

nets:
  N1: Eleman1.GND, R2.Pin_1
  N2: Eleman1.A0, R2.Pin_0
