# Fritzing sketch gy_NodeMCU_KY040_Rotary_Encoder (saved by Fritzing 0.9.2b)
breadboards: 1

parts:
  U1 = NodeMCU V3.0
  ENCODER1 = Rotary Encoder with switch (KY-040) [part_number=KY-040]

nets:
  N1: U1.D2, ENCODER1.CLK
  N2: U1.D3, ENCODER1.DT
  N3: U1.D4, ENCODER1.SW
  N4: U1.GND#6, U1.GND#13, U1.GND#16, U1.GND#33
  N5: U1.VU, U1.GND#41, ENCODER1.GND, ENCODER1.+

custom parts:
  NodeMCU V3.0: ESP8266 based NodeMCU
  Rotary Encoder with switch (KY-040): A Rotary Encoder with switch
