# Fritzing sketch NodeMcu_wifi_Car (saved by Fritzing 0.9.2b)
breadboards: 1

parts:
  U1 = NodeMCU V3.0
  VCC1 = Battery
  S1 = H-Bridge with L298N
  M1 = DC Motor
  M2 = DC Motor
  LED1 = smd LED [color="Red (633nm)" package="0603 [SMD]"]
  LED2 = smd LED [color="Red (633nm)" package="0603 [SMD]"]
  LED3 = smd LED [color="Red (633nm)" package="0603 [SMD]"]
  LED4 = smd LED [color="Red (633nm)" package="0603 [SMD]"]
  R1 = Resistor [tolerance=±5% resistance=220 package=THT]
  R2 = Resistor [tolerance=±5% resistance=220 package=THT]
  R3 = Resistor [tolerance=±5% resistance=220 package=THT]
  R4 = Resistor [tolerance=±5% resistance=220 package=THT]

nets:
  N1: U1.D1, S1.ENA
  N2: U1.D2, S1.IN1
  N3: U1.D3, S1.IN2
  N4: U1.D4, S1.IN3
  N5: U1.GND#6, U1.GND#13, U1.GND#16, U1.GND#33, VCC1.-, S1.12V, R1.Pin_0, R2.Pin_0, R3.Pin_0, R4.Pin_0
  N6: U1.D5, S1.IN4
  N7: U1.D6, S1.ENB
  N8: U1.D7, LED2.anode
  N9: U1.D8, LED1.anode
  N10: U1.RX, LED3.anode
  N11: U1.TX, LED4.anode
  VIN: U1.Vin, VCC1.+, S1.GND
  N12: S1.M1-01, M1.pin_2
  N13: S1.M1-02, M1.pin_1
  N14: S1.M2-01, M2.pin_2
  N15: S1.M2-02, M2.pin_1
  N16: LED1.cathode, R1.Pin_1
  N17: LED2.cathode, R2.Pin_1
  N18: LED3.cathode, R3.Pin_1
  N19: LED4.cathode, R4.Pin_1

custom parts:
  NodeMCU V3.0: ESP8266 based NodeMCU
  Battery: Your standard 2x 18650 battery pack (7,4 Volts)
  H-Bridge with L298N: h-bridge
