# Fritzing sketch resetbuton (saved by Fritzing 0.9.3b)
breadboards: 1

parts:
  Parça1 = Arduino Mega 2560 (Rev3)
  S1 = Momentary Switch [package=ksa_sealed_tac_switch]

nets:
  N1: Parça1.RESET, S1.3, S1.4
  N2: Parça1.GND, S1.1, S1.2
