# Fritzing sketch gy_robot_orumcek (saved by Fritzing 0.9.2b)
breadboards: 1

parts:
  Eleman1 = Arduino Nano (Rev3.0)
  12 = Basic Servo
  11 = Basic Servo
  13 = Basic Servo
  7 = Basic Servo
  5 = Basic Servo
  6 = Basic Servo
  10 = Basic Servo
  8 = Basic Servo
  9 = Basic Servo
  3 = Basic Servo
  2 = Basic Servo
  4 = Basic Servo
  18650x2_=_7_4_Volt = Battery Holders [package=battery-aa-kit]
  D1 = Rectifier Diode [part_number=1N4001 package="Melf DO-213 AB [SMD]"]
  S1 = SPST Switch [package=switch-spdt-smd]  # not connected
  F1 = FUSE [package=fuse_5mm]

nets:
  GND: Eleman1.GND, 12.gnd, 11.gnd, 13.gnd, 7.gnd, 5.gnd, 6.gnd, 10.gnd, 8.gnd, 9.gnd, 3.gnd, 2.gnd, 4.gnd, 18650x2_=_7_4_Volt.-
  N1: Eleman1.D2, 2.pulse
  N2: Eleman1.D3, 3.pulse
  N3: Eleman1.D4, 4.pulse
  N4: Eleman1.D5, 5.pulse
  N5: Eleman1.D6, 6.pulse
  N6: Eleman1.D7, 7.pulse
  N7: Eleman1.D8, 8.pulse
  N8: Eleman1.D9, 9.pulse
  N9: Eleman1.D10, 10.pulse
  N10: Eleman1.D11/MOSI, 11.pulse
  N11: Eleman1.D12/MISO, 12.pulse
  VCC: Eleman1.VIN, 12.vcc, 11.vcc, 13.vcc, 7.vcc, 5.vcc, 6.vcc, 10.vcc, 8.vcc, 9.vcc, 3.vcc, 2.vcc, 4.vcc, D1.cathode
  N12: Eleman1.D13/SCK, 13.pulse
  N13: 18650x2_=_7_4_Volt.+, F1.1
