# Fritzing sketch gy_Robotics_2 (saved by Fritzing 0.9.3b)

parts:
  Parça1 = Arduino Mega 2560 (Rev3)
  J1 = Basic Servo
  J2 = Basic Servo
  J3 = Basic Servo
  J4 = Basic Servo
  Servo_0 = Basic Servo
  BAT1 = Battery Holders [package=battery-aaa]
  U2 = POT [package=alps_pot]  # not connected
  U3 = POT [package=alps_pot]
  U4 = POT [package=alps_pot]
  U5 = POT [package=alps_pot]
  U6 = POT [package=alps_pot]
  R0_(10K) = POT [package=alps_pot]
  J5 = Basic Servo

nets:
  N1: Parça1.A0, R0_(10K).S
  N2: Parça1.A1, U6.S
  N3: Parça1.A2, U5.S
  N4: Parça1.A3, U4.S
  N5: Parça1.A4, U3.S
  N6: Parça1.D2_PWM, Servo_0.pulse
  N7: Parça1.D3_PWM, J4.pulse
  N8: Parça1.D4_PWM, J3.pulse
  N9: Parça1.D5_PWM, J2.pulse
  N10: Parça1.D6_PWM, J1.pulse
  N11: Parça1.D7_PWM, J5.pulse
  N12: J1.gnd, BAT1.-
  N13: BAT1.+, J5.vcc
