# Fritzing sketch role_buton (saved by Fritzing 0.9.3b)
breadboards: 1

parts:
  S1 = Pushbutton [package="[THT]"]
  Parça1 = Arduino Mega ADK (Rev3)
  U1 = 2-Channel 5v Relay Shield [package=relay-2ch5v10a]
  VCC1 = Battery

nets:
  N1: S1.Pin_1, S1.Pin_2, Parça1.D3_PWM
  GND: S1.Pin_3, S1.Pin_4, Parça1.GND, U1.GND, VCC1.-
  N2: Parça1.D2_PWM, U1.IN1
  N3: U1.VCC, VCC1.+

custom parts:
  2-Channel 5v Relay Shield: 2 Channel 5v Relay Shield w. 2x SPD-06VDC-SD-C
