# Fritzing sketch gy_GunesTakip (saved by Fritzing 0.9.3b)
breadboards: 1

parts:
  R1 = Resistor [tolerance=±5% resistance=220 package=THT]
  R2 = Photocell (LDR) [package=THT]
  R3 = Photocell (LDR) [package=THT]
  R4 = Photocell (LDR) [package=THT]
  R5 = Photocell (LDR) [package=THT]
  R6 = Resistor [tolerance=±5% resistance=220 package=THT]
  R7 = Resistor [tolerance=±5% resistance=220 package=THT]
  part = Resistor [tolerance=±5% resistance=10k package=THT]
  J1 = Basic Servo
  J2 = Basic Servo
  U1 = BATTERY-2 [package=battery-aa]
  Parça1 = Arduino Mega ADK (Rev3)

nets:
  N1: R1.Pin_0, R2.pin_1, Parça1.A3
  GND: R1.Pin_1, R6.Pin_1, R7.Pin_1, part.Pin_1, J1.gnd, J2.gnd, U1.-1, Parça1.GND
  N2: R2.pin_0, R3.pin_0, R4.pin_0, R5.pin_0, Parça1.5V
  N3: R3.pin_1, R6.Pin_0, Parça1.A2
  N4: R4.pin_1, R7.Pin_0, Parça1.A1
  N5: R5.pin_1, part.Pin_0, Parça1.A0
  VCC: J1.vcc, J2.vcc, U1.+1
  N6: J1.pulse, Parça1.D10_PWM
  N7: J2.pulse, Parça1.D9_PWM
