# Fritzing sketch HSCR04 (saved by Fritzing 0.9.2b)

parts:
  Eleman1 = SRF05 Ultrasonic Rangefinder
  Eleman2 = Arduino Nano (Rev3.0)

nets:
  VCC: Eleman1.VCC, Eleman2.5V
  N1: Eleman1.Trig, Eleman2.D4
  N2: Eleman1.Echo, Eleman2.D5
  GND: Eleman1.GND, Eleman2.GND
