# Fritzing sketch gy_color_sensor_tsc230 (saved by Fritzing 0.9.2b)
breadboards: 1

parts:
  Eleman1 = Arduino Nano (Rev3.0)
  Servo_a = Basic Servo
  Servo_b = Basic Servo
  e-radionica1 = TCS230 Color Sensor [part_number=101209]

nets:
  N1: Eleman1.D3, e-radionica1.OE
  N2: Eleman1.D4, e-radionica1.S1
  N3: Eleman1.D5, e-radionica1.S0
  N4: Eleman1.D6, e-radionica1.S3
  N5: Eleman1.D7, e-radionica1.S2
  N6: Eleman1.D8, e-radionica1.Out
  N7: Eleman1.D9, Servo_a.pulse
  N8: Eleman1.D10, Servo_b.pulse
  5V: Eleman1.5V, e-radionica1.Vcc
  GND: Servo_a.gnd, Servo_b.gnd, e-radionica1.Gnd
  VCC: Servo_a.vcc, Servo_b.vcc

custom parts:
  TCS230 Color Sensor: TCS230
