# Fritzing sketch gy_joystick (saved by Fritzing 0.9.2b)

parts:
  Eleman1 = Arduino Mega 2560 (Rev3)
  Eleman2 = Thumb Joystick

nets:
  N1: Eleman1.A1, Eleman2.VERT
  N2: Eleman1.A2, Eleman2.HORZ
  N3: Eleman1.D10_PWM, Eleman2.SEL
  5V: Eleman1.5V, Eleman2.VCC
  GND: Eleman1.GND, Eleman2.GND
