# Fritzing sketch gy_joystick_nano (saved by Fritzing 0.9.2b)

parts:
  Eleman2 = Thumb Joystick
  Eleman3 = Arduino Nano (Rev3.0)

nets:
  GND: Eleman2.GND, Eleman3.GND
  N1: Eleman2.SEL, Eleman3.D10
  N2: Eleman2.HORZ, Eleman3.A2
  N3: Eleman2.VERT, Eleman3.A1
  VCC: Eleman2.VCC, Eleman3.5V
