# Fritzing sketch ss49e_nano (saved by Fritzing 0.9.3b)

parts:
  Parça1 = Arduino Nano (Rev3.0)
  Q1 = PNP-Transistor [package="TO92 [THT]"]

nets:
  N1: Parça1.GND, Q1.B
  N2: Parça1.5V, Q1.E
  N3: Parça1.A0, Q1.C
