# Fritzing sketch potansiyometre (saved by Fritzing 0.9.2b)

parts:
  Eleman1 = Arduino Mega 2560 (Rev3)
  R1 = Rotary Potentiometer (Large) [maximum_resistance=10kΩ package=THT]

nets:
  N1: Eleman1.A2, R1.wiper
  N2: Eleman1.5V, R1.leg2
  N3: Eleman1.GND, R1.leg1
