# Fritzing sketch servo (saved by Fritzing 0.9.3b)
breadboards: 1

parts:
  Parça1 = Arduino Mega ADK (Rev3)
  J1 = Basic Servo
  Parça2 = Thumb Joystick
  VCC1 = Battery

nets:
  N1: Parça1.A0, Parça2.VERT
  N2: Parça1.D9_PWM, J1.pulse
  5V: Parça1.5V, Parça2.VCC
  GND: Parça1.GND, J1.gnd, Parça2.GND, VCC1.-
  N3: J1.vcc, VCC1.+
