# Fritzing sketch gy_Termistor (saved by Fritzing 0.9.2b)

parts:
  R3 = Temperature Sensor (Thermistor) [thermistor_type=NTC package=THT]  # not connected
  10K = Temperature Sensor (Thermistor) [thermistor_type=NTC package=THT]
  Eleman1 = Arduino Nano (Rev3.0)
  R5 = Resistor [tolerance=±5% resistance=220 package=THT]
  part = Resistor [tolerance=±5% resistance=10k package=THT]

nets:
  N1: 10K.pin_0, Eleman1.5V
  N2: 10K.pin_1, Eleman1.A0, part.Pin_0
  N3: Eleman1.GND, R5.Pin_1, part.Pin_1
  N4: Eleman1.A1, R5.Pin_0
